// Logisim project B127.circ as structural Verilog: 2 circuits, main circuit main
module main (
  input  [7:0] LDR_STR_ALU,
  output [7:0] RegData1,
  output [7:0] RegData2
);

  wire and_1_out, and_2_out, and_3_out, and_4_out, clock_1_out, decoder_1_out0, decoder_1_out1,
       decoder_1_out2, decoder_1_out3, not_1_out, not_2_out;
  wire [1:0] multiplexer_4_out;
  wire [3:0] ram_1_dout, ram_1_dout_2, ram_1_dout_3, ram_1_dout_4;
  wire [7:0] adder_1_out, adder_2_out, adder_3_out, multiplexer_3_out, multiplexer_5_out, multiplexer_6_out,
       multiplier_1_out, PC_q, ram_2_dout, X0_q, X1_q, X2_q, X3_q;

  Adder adder_1 (.a(PC_q), .b(8'h1), .out(adder_1_out));  // open: cin, cout
  Register PC (.D(adder_1_out), .en(1'b1), .clk(clock_1_out), .Q(PC_q));  // open: clr
  Clock clock_1 (.out(clock_1_out));
  RAM #(.dataWidth(16), .enables("line")) ram_1 (
    .addr(PC_q), .we(1'b0), .clk(clock_1_out), .dout({ram_1_dout_2, ram_1_dout, ram_1_dout_4, ram_1_dout_3}));  // open: din
  Decoder #(.select(2)) decoder_1 (
    .out0(decoder_1_out0), .out1(decoder_1_out1), .out2(decoder_1_out2), .out3(decoder_1_out3),
    .sel(ram_1_dout[2:1]));  // open: en
  Hex_Digit_Display hex_digit_display_1 (.value(ram_1_dout_2));  // open: dp
  Hex_Digit_Display hex_digit_display_2 (.value(ram_1_dout));  // open: dp
  Hex_Digit_Display hex_digit_display_3 (.value(ram_1_dout_4));  // open: dp
  and and_1 (and_1_out, ram_1_dout_2[0], decoder_1_out0);
  and and_2 (and_2_out, ram_1_dout_2[0], decoder_1_out1);
  and and_3 (and_3_out, ram_1_dout_2[0], decoder_1_out2);
  and and_4 (and_4_out, ram_1_dout_2[0], decoder_1_out3);
  Hex_Digit_Display hex_digit_display_4 (.value(ram_1_dout_3));  // open: dp
  Register X0 (.D(multiplexer_5_out), .en(and_1_out), .clk(clock_1_out), .Q(X0_q));  // open: clr
  Register X1 (.D(multiplexer_5_out), .en(and_2_out), .clk(clock_1_out), .Q(X1_q));  // open: clr
  Register X2 (.D(multiplexer_5_out), .en(and_3_out), .clk(clock_1_out), .Q(X2_q));  // open: clr
  Register X3 (.D(multiplexer_5_out), .en(and_4_out), .clk(clock_1_out), .Q(X3_q));  // open: clr
  Multiplexer #(.select(2), .width(8)) multiplexer_1 (
    .in0(X0_q), .in1(X1_q), .in2(X2_q), .in3(X3_q), .out(RegData1), .sel({ram_1_dout[0], ram_1_dout_4[3]}));
  Adder adder_2 (.a(RegData1), .b(RegData2), .out(adder_2_out));  // open: cin, cout
  Multiplier multiplier_1 (.a(RegData1), .b(RegData2), .out(multiplier_1_out));  // open: cin, cout
  Multiplexer #(.select(2), .width(8)) multiplexer_2 (
    .in0(X0_q), .in1(X1_q), .in2(X2_q), .in3(X3_q), .out(RegData2), .sel(multiplexer_4_out));
  Adder adder_3 (.a({1'b0, ram_1_dout_4[2:0], ram_1_dout_3}), .b(RegData1), .out(adder_3_out));  // open: cin, cout
  Multiplexer #(.width(8)) multiplexer_3 (
    .in0(adder_2_out), .in1(multiplier_1_out), .out(multiplexer_3_out), .sel(not_1_out));
  not not_1 (not_1_out, ram_1_dout[3]);
  LED led_1 (.in(ram_1_dout_2[3]));
  LED led_2 (.in(ram_1_dout_2[0]));
  Multiplexer #(.width(2)) multiplexer_4 (
    .in0(ram_1_dout_4[2:1]), .in1(ram_1_dout[2:1]), .out(multiplexer_4_out), .sel(ram_1_dout_2[2]));
  not not_2 (not_2_out, ram_1_dout_2[3]);
  Multiplexer #(.width(8)) multiplexer_5 (
    .in0(ram_2_dout), .in1(multiplexer_3_out), .out(multiplexer_5_out), .sel(not_2_out));
  Multiplexer #(.width(8)) multiplexer_6 (
    .in0(LDR_STR_ALU), .in1(RegData2), .out(multiplexer_6_out), .sel(ram_1_dout_2[2]));
  LED led_3 (.in(ram_1_dout_2[1]));
  LED led_4 (.in(ram_1_dout[3]));
  RAM #(.enables("line")) ram_2 (
    .addr(adder_3_out), .we(ram_1_dout_2[2]), .clk(clock_1_out), .din(multiplexer_6_out), .dout(ram_2_dout));
  // RGBLED rgbled_1: pin names not known; wires that end beside it: 1'b0, not_2_out, ram_1_dout[3]

  // Notes on the sheet:
  //   RegDataW value wire coming back
  //   WriteReg signal wire  into decoder
  //   Regwrite signal value wire
  //   Instruction Memory
  //   immediate value reverse splitter
  //   RegData1 value wire
  //   splitter for reading opcodes and everything else
  //   ADD
  //   MUL
  //   offset calc(adds imm + address)
  //   ADD/MUL ALU
  //   ReadReg1 wire value
  //   RegData2 value wire
  //   ReadReg2 wire value
  //   On:Green
  //   Off:Red
  //   On:Green
  //   Off:Red
  //   A/M/L/S ALUout
  //   On:Green
  //   Off:Red
  //   On:Green
  //   Off:Red
  //   Data Memory
  //   Led comapring bit 15, and bit 11
  //   if memtoReg(bit 15): 1, alutout(bit 11):1  = yellow,    if memtoreg(bit 15): 0 , aluout(bit 11): 1 = red, if memtoreg(bit 15):1 , alutout(bit 11):0 = green
endmodule

module registerfile (
  input  Clock,
  input  [1:0] WriteReg,
  input  [7:0] RegDataW,
  input  [1:0] ReadReg1,
  input  RegWrite,
  input  [1:0] ReadReg2,
  output [7:0] RegData1,
  output [7:0] RegData2
);

  wire and_1_out, and_2_out, and_3_out, and_4_out, decoder_1_out0, decoder_1_out1, decoder_1_out2,
       decoder_1_out3;
  wire [7:0] X0_q, X1_q, X2_q, X3_q;

  Decoder #(.select(2)) decoder_1 (
    .out0(decoder_1_out0), .out1(decoder_1_out1), .out2(decoder_1_out2), .out3(decoder_1_out3), .sel(WriteReg));  // open: en
  Register X0 (.D(RegDataW), .en(and_1_out), .clk(Clock), .Q(X0_q));  // open: clr
  and and_1 (and_1_out, RegWrite, decoder_1_out0);
  and and_2 (and_2_out, RegWrite, decoder_1_out1);
  and and_3 (and_3_out, RegWrite, decoder_1_out2);
  and and_4 (and_4_out, RegWrite, decoder_1_out3);
  Register X1 (.D(RegDataW), .en(and_2_out), .clk(Clock), .Q(X1_q));  // open: clr
  Register X2 (.D(RegDataW), .en(and_3_out), .clk(Clock), .Q(X2_q));  // open: clr
  Register X3 (.D(RegDataW), .en(and_4_out), .clk(Clock), .Q(X3_q));  // open: clr
  Multiplexer #(.select(2), .width(8)) multiplexer_1 (
    .in0(X0_q), .in1(X1_q), .in2(X2_q), .in3(X3_q), .out(RegData1), .sel(ReadReg1));
  Multiplexer #(.select(2), .width(8)) multiplexer_2 (
    .in0(X0_q), .in1(X1_q), .in2(X2_q), .in3(X3_q), .out(RegData2), .sel(ReadReg2));
endmodule
