// Logisim project cpu.circ as structural Verilog: 2 circuits, main circuit main
module main (
  input  in_1,
  output [7:0] out_2
);

  wire clock_1_out, undriven;
  wire [1:0] registerfile_1_p1, registerfile_1_p2, registerfile_1_p4;
  wire [1:1] registerfile_1_p3;
  wire [7:0] adder_1_out, adder_2_out, multiplexer_1_out, register_1_q, registerfile_1_p5, subtractor_1_out;

  Adder adder_1 (.a(register_1_q), .b(8'h1), .out(adder_1_out));  // open: cin, cout
  Register register_1 (.D(adder_1_out), .en(1'b1), .clk(clock_1_out), .Q(register_1_q));  // open: clr
  Clock clock_1 (.out(clock_1_out));
  RAM ram_1 (.addr(register_1_q), .we(1'b0), .oe(1'b1), .clk(undriven), .dout(out_2));  // open: din
  // registerfile registerfile_1: pin names not known; wires that end beside it: registerfile_1_p1, registerfile_1_p2, {registerfile_1_p3[1], in_1}, registerfile_1_p4, registerfile_1_p5, registerfile_1_p5
  Adder adder_2 (.a(registerfile_1_p5), .b(registerfile_1_p5), .out(adder_2_out));  // open: cin, cout
  Subtractor subtractor_1 (.a(registerfile_1_p5), .b(registerfile_1_p5), .out(subtractor_1_out));  // open: bin, bout
  Multiplexer #(.width(8)) multiplexer_1 (
    .in0(adder_2_out), .in1(subtractor_1_out), .out(multiplexer_1_out), .sel(in_1));
endmodule

module registerfile (
  input  [1:0] WriteReg,
  input  [7:0] RegDataW,
  input  [1:0] ReadReg1,
  input  RegWrite,
  input  [1:0] ReadReg2,
  output [7:0] RegData1,
  output [7:0] RegData2
);

  wire and_1_out, and_2_out, and_3_out, and_4_out, CIock_out, decoder_1_out0, decoder_1_out1, decoder_1_out2,
       decoder_1_out3;
  wire [7:0] X0_q, X1_q, X2_q, X3_q;

  Clock CIock (.out(CIock_out));
  Decoder #(.select(2)) decoder_1 (
    .out0(decoder_1_out0), .out1(decoder_1_out1), .out2(decoder_1_out2), .out3(decoder_1_out3), .sel(WriteReg));  // open: en
  Register X0 (.D(RegDataW), .en(and_1_out), .clk(CIock_out), .Q(X0_q));  // open: clr
  and and_1 (and_1_out, RegWrite, decoder_1_out0);
  and and_2 (and_2_out, RegWrite, decoder_1_out1);
  and and_3 (and_3_out, RegWrite, decoder_1_out2);
  and and_4 (and_4_out, RegWrite, decoder_1_out3);
  Register X1 (.D(RegDataW), .en(and_2_out), .clk(CIock_out), .Q(X1_q));  // open: clr
  Register X2 (.D(RegDataW), .en(and_3_out), .clk(CIock_out), .Q(X2_q));  // open: clr
  Register X3 (.D(RegDataW), .en(and_4_out), .clk(CIock_out), .Q(X3_q));  // open: clr
  Multiplexer #(.select(2), .width(8)) multiplexer_1 (
    .in0(X0_q), .in1(X1_q), .in2(X2_q), .in3(X3_q), .out(RegData1), .sel(ReadReg1));
  Multiplexer #(.select(2), .width(8)) multiplexer_2 (
    .in0(X0_q), .in1(X1_q), .in2(X2_q), .in3(X3_q), .out(RegData2), .sel(ReadReg2));
endmodule
